// Logisim project 7LABZANIN.circ as structural Verilog: 5 circuits, main circuit main
module main (
  output [7:0] out_1
);

  wire and_1_out, clock_1_out, not_1_out;
  wire [1:0] ram_1_data;
  wire [2:0] counter_1_q;
  wire [7:0] adder_1_out, ram_2_data;

  Counter #(.width(3), .max('h7)) counter_1 (.Q(counter_1_q), .clk(clock_1_out));  // open: load, D, count, carry, clr
  Clock clock_1 (.out(clock_1_out));
  not not_1 (not_1_out, clock_1_out);
  RAM #(.addrWidth(3), .dataWidth(2), .bus("separate")) ram_1 (
    .addr(counter_1_q), .data(ram_1_data));  // open: din, str, sel, clk, ld, clr
  RAM #(.addrWidth(3), .bus("separate")) ram_2 (
    .addr(counter_1_q), .din(out_1), .data(ram_2_data), .clk(ram_1_data[1]));  // open: str, sel, ld, clr
  Adder adder_1 (.a(out_1), .b(ram_2_data), .out(adder_1_out));  // open: cin, cout
  and and_1 (and_1_out, ram_1_data[0], not_1_out);
  Register register_1 (.D(adder_1_out), .Q(out_1), .clk(and_1_out));  // open: en, clr
endmodule

// A
module \АЛУ  (
  input  [7:0] in_1,
  input  [7:0] B,
  input  in_3,
  input  [2:0] in_4,
  output Overflow,
  output [7:0] out_6,
  output Zero_flag
);

  wire not_1_out, or_2_out;
  wire [7:0] adder_1_out, and_1_out, multiplexer_1_out, multiplexer_2_out, not_2_out, or_1_out,
       subtractor_1_out;

  not not_1 (not_1_out, in_3);
  Multiplexer #(.width(8)) multiplexer_1 (.in0(in_1), .in1(B), .out(multiplexer_1_out), .sel(in_3));  // open: en
  Multiplexer #(.width(8)) multiplexer_2 (.in0(in_1), .in1(B), .out(multiplexer_2_out), .sel(not_1_out));  // open: en
  Adder adder_1 (.a(multiplexer_1_out), .b(multiplexer_2_out), .out(adder_1_out), .cout(Overflow));  // open: cin
  Subtractor subtractor_1 (.a(multiplexer_1_out), .b(multiplexer_2_out), .out(subtractor_1_out));  // open: bin, bout
  assign and_1_out = multiplexer_1_out & multiplexer_2_out;  // AND_Gate and_1, 8 bits wide
  assign or_1_out = multiplexer_1_out | multiplexer_2_out;  // OR_Gate or_1, 8 bits wide
  assign not_2_out = ~multiplexer_1_out;  // NOT_Gate not_2, 8 bits wide
  Multiplexer #(.select(3), .width(8), .enable("false")) multiplexer_3 (
    .in0({8{1'b0}}), .in1(adder_1_out), .in2(subtractor_1_out), .in3(and_1_out), .in4(or_1_out),
    .in5(not_2_out), .out(out_6), .sel(in_4));  // open: in6, in7
  not not_3 (Zero_flag, or_2_out);
  or or_2 (or_2_out, out_6[3], out_6[0], out_6[1], out_6[2], out_6[4], out_6[5], out_6[6], out_6[7]);
endmodule

module \ФН  (
  input  [2:0] in_1,
  output out_2,
  output [7:0] out_3,
  output out_4
);

  wire and_1_out, and_2_out, button_1_out, button_2_out, clock_1_out, not_1_out, not_2_out, not_3_out;
  wire [3:0] ADRESS_q, counter_1_q, counter_2_q, INSTRUCTION_q, multiplexer_1_out, ram_2_data;
  wire [7:0] multiplexer_2_out, ram_1_data, TEMP_q, \алу_1_p6 ;
  wire [7:4] ram_2_data_2;

  Clock clock_1 (.out(clock_1_out));
  Counter #(.width(4), .max('hf)) counter_1 (
    .load(INSTRUCTION_q[3]), .D(ADRESS_q), .count(not_1_out), .Q(counter_1_q), .clk(clock_1_out),
    .clr(button_2_out));  // open: carry
  not not_1 (not_1_out, INSTRUCTION_q[3]);
  not not_2 (not_2_out, clock_1_out);
  Multiplexer #(.width(4), .enable("false")) multiplexer_1 (
    .in0(counter_1_q), .in1(ADRESS_q), .out(multiplexer_1_out), .sel(not_2_out));
  and and_1 (and_1_out, clock_1_out, INSTRUCTION_q[1]);
  RAM #(.addrWidth(4), .bus("separate")) ram_1 (
    .addr(multiplexer_1_out), .din(out_3), .data(ram_1_data), .clk(and_1_out));  // open: str, sel, ld, clr
  Register #(.width(4)) ADRESS (.D(ram_1_data[3:0]), .Q(ADRESS_q), .clk(not_2_out), .clr(button_2_out));  // open: en
  not not_3 (not_3_out, ram_2_data_2[7]);
  Button button_1 (.out(button_1_out));
  Register #(.trigger("falling")) TEMP (.D(ram_1_data), .Q(TEMP_q), .clk(and_2_out), .clr(button_2_out));  // open: en
  and and_2 (and_2_out, INSTRUCTION_q[0], not_2_out);
  Button button_2 (.out(button_2_out));
  Register #(.width(4)) INSTRUCTION (
    .D(ram_1_data[7:4]), .Q(INSTRUCTION_q), .clk(not_2_out), .clr(button_2_out));  // open: en
  Counter #(.width(4), .max('hf)) counter_2 (
    .load(ram_2_data_2[7]), .D(ram_2_data), .count(not_3_out), .Q(counter_2_q), .clk(button_1_out));  // open: carry, clr
  // Probe on TEMP_q
  // Probe on out_3
  RAM #(.addrWidth(4), .bus("separate")) ram_2 (
    .addr(counter_2_q), .data({ram_2_data_2, ram_2_data}));  // open: din, str, sel, clk, ld, clr
  // Probe on ram_2_data_2
  // Probe on \алу_1_p6 
  // АЛУ_2 алу_1: pin names not known; wires that end beside it: out_3, TEMP_q, clock_1_out, in_1, out_2, \алу_1_p6 , out_4
  Multiplexer #(.width(8)) multiplexer_2 (
    .in0(\алу_1_p6 ), .in1(TEMP_q), .out(multiplexer_2_out), .sel(INSTRUCTION_q[2]));  // open: en
  Register #(.trigger("falling")) ACCUM (
    .D(multiplexer_2_out), .Q(out_3), .clk(clock_1_out), .clr(button_2_out));  // open: en
  Decoder #(.select(4)) decoder_1 ();  // open: out0, out1, out2, out3, out4, out5, out6, out7, out8, out9, out10, out11, out12, out13, out14, out15, sel, en
endmodule

module \АЛУ_2  (
  input  [7:0] in_1,
  input  [7:0] B,
  input  [3:0] in_3,
  output Overflow,
  output [7:0] out_5,
  output Zero_flag
);

  wire not_1_out, or_2_out;
  wire [7:0] adder_1_out, and_1_out, multiplexer_1_out, multiplexer_2_out, not_2_out, or_1_out,
       subtractor_1_out;

  not not_1 (not_1_out, 1'b0);
  Multiplexer #(.width(8)) multiplexer_1 (.in0(in_1), .in1(B), .out(multiplexer_1_out), .sel(1'b0));  // open: en
  Multiplexer #(.width(8)) multiplexer_2 (.in0(in_1), .in1(B), .out(multiplexer_2_out), .sel(not_1_out));  // open: en
  Adder adder_1 (.a(multiplexer_1_out), .b(multiplexer_2_out), .out(adder_1_out), .cout(Overflow));  // open: cin
  Subtractor subtractor_1 (.a(multiplexer_1_out), .b(multiplexer_2_out), .out(subtractor_1_out));  // open: bin, bout
  assign and_1_out = multiplexer_1_out & multiplexer_2_out;  // AND_Gate and_1, 8 bits wide
  assign or_1_out = multiplexer_1_out | multiplexer_2_out;  // OR_Gate or_1, 8 bits wide
  assign not_2_out = ~multiplexer_1_out;  // NOT_Gate not_2, 8 bits wide
  Multiplexer #(.select(4), .width(8), .enable("false")) multiplexer_3 (
    .in0({8{1'b0}}), .in1(adder_1_out), .in2(subtractor_1_out), .in3(and_1_out), .in4(or_1_out),
    .in5(not_2_out), .in6({8{1'b0}}), .in7({8{1'b0}}), .in8({8{1'b0}}), .in9({8{1'b0}}), .in10({8{1'b0}}),
    .in11({8{1'b0}}), .in12({8{1'b0}}), .in13({8{1'b0}}), .in14({8{1'b0}}), .in15({8{1'b0}}), .out(out_5),
    .sel(in_3));
  or or_2 (or_2_out, out_5[3], out_5[0], out_5[1], out_5[2], out_5[4], out_5[5], out_5[6], out_5[7]);
  not not_3 (Zero_flag, or_2_out);
endmodule

module \ФН_2  (
  output out_1,
  output [7:0] out_2,
  output out_3
);

  wire and_1_out, and_2_out, button_1_out, clock_1_out, decoder_1_out1, decoder_1_out2, decoder_1_out3,
       decoder_1_out4, decoder_1_out5, decoder_1_out6, decoder_1_out7, decoder_1_out8, not_1_out, not_2_out,
       or_1_out;
  wire [3:0] ADRESS_q, counter_1_q, INSTRUCTION_q, multiplexer_1_out;
  wire [7:0] multiplexer_2_out, ram_1_data, TEMP_q, \алу_1_out_5 ;

  Clock clock_1 (.out(clock_1_out));
  Counter #(.width(4), .max('hf)) counter_1 (
    .load(decoder_1_out8), .D(ADRESS_q), .count(not_1_out), .Q(counter_1_q), .clk(clock_1_out),
    .clr(button_1_out));  // open: carry
  not not_1 (not_1_out, decoder_1_out8);
  not not_2 (not_2_out, clock_1_out);
  Multiplexer #(.width(4), .enable("false")) multiplexer_1 (
    .in0(counter_1_q), .in1(ADRESS_q), .out(multiplexer_1_out), .sel(not_2_out));
  and and_1 (and_1_out, clock_1_out, decoder_1_out6);
  RAM #(.addrWidth(4), .bus("separate")) ram_1 (
    .addr(multiplexer_1_out), .din(out_2), .data(ram_1_data), .clk(and_1_out));  // open: str, sel, ld, clr
  Register #(.width(4)) ADRESS (.D(ram_1_data[3:0]), .Q(ADRESS_q), .clk(not_2_out), .clr(button_1_out));  // open: en
  Register #(.trigger("falling")) TEMP (.D(ram_1_data), .Q(TEMP_q), .clk(and_2_out), .clr(button_1_out));  // open: en
  and and_2 (and_2_out, or_1_out, not_2_out);
  Button button_1 (.out(button_1_out));
  Register #(.width(4)) INSTRUCTION (
    .D(ram_1_data[7:4]), .Q(INSTRUCTION_q), .clk(not_2_out), .clr(button_1_out));  // open: en
  // Probe on TEMP_q
  // Probe on out_2
  Decoder #(.select(4), .enable("false")) decoder_1 (
    .out1(decoder_1_out1), .out2(decoder_1_out2), .out3(decoder_1_out3), .out4(decoder_1_out4),
    .out5(decoder_1_out5), .out6(decoder_1_out6), .out7(decoder_1_out7), .out8(decoder_1_out8),
    .sel(INSTRUCTION_q));  // open: out0, out9, out10, out11, out12, out13, out14, out15
  // Probe on \алу_1_out_5 
  \АЛУ_2  \u_алу_1  (
    .in_1(TEMP_q), .B(out_2), .in_3(INSTRUCTION_q), .Overflow(out_1), .out_5(\алу_1_out_5 ), .Zero_flag(out_3));
  Multiplexer #(.width(8)) multiplexer_2 (
    .in0(\алу_1_out_5 ), .in1(TEMP_q), .out(multiplexer_2_out), .sel(decoder_1_out7));  // open: en
  Register #(.trigger("falling")) ACCUM (
    .D(multiplexer_2_out), .Q(out_2), .clk(clock_1_out), .clr(button_1_out));  // open: en
  or or_1 (or_1_out, decoder_1_out1, decoder_1_out2, decoder_1_out3, decoder_1_out4, decoder_1_out5, decoder_1_out7);

  // Notes on the sheet:
  //   1- сложение
  //   2 - вычитание
  //   3- и
  //   4-или
  //   5-не
  //   6-запись в озу
  //   7-запись в аккум
  //   8-безусловный переход
endmodule
